# Fritzing sketch Circuit Diagram (saved by Fritzing 0.9.4)
breadboards: 1

parts:
  SW1 = DIP Switch 8 Position [package=dipswitch-08]
  LED1 = LEDs [package=led10mm]
  R1 = Resistor [tolerance=±5% resistance=220 package="1206 [SMD]"]
  U5 = 7400 4 x 2 Input NAND Gate [part_number=7400 package="DIP (Dual Inline) [THT]"]
  U6 = 7400 4 x 2 Input NAND Gate [part_number=7400 package="DIP (Dual Inline) [THT]"]

nets:
  Input C: SW1.6
  Input B: SW1.7
  Input A: SW1.8
  5V: SW1.9, SW1.10, SW1.11, U5.VDD, U6.VDD
  N1: LED1.A, R1.Pin_0
  GND: U5.GND, U6.GND
